# Fritzing sketch esquematico_electro (saved by Fritzing 0.9.3b)
breadboards: 1

parts:
  Componente1 = BluePill
  LCD1 = TFT 1.8 inch 160x128 w SD
  J1 = Piezo Speaker
  R1 = Temperature Sensor (Thermistor) [thermistor_type=NTC package=THT]
  R2 = Resistor [tolerance=±5% resistance=10k package=THT]
  Q1 = Basic FET P-Channel [package="D2Pak [SMD]"]
  S1 = SWITCH-MOMENTARY-2 [package=tactile-pth-12mm]
  Q2 = Basic FET P-Channel [package="D2Pak [SMD]"]
  R3 = Resistor [tolerance=±5% resistance=10k package=THT]
  D1 = Diode [package=diode-hv]
  S2 = SWITCH-MOMENTARY-2 [package=tactile-pth-12mm]
  S3 = SWITCH-MOMENTARY-2 [package=tactile-pth-12mm]
  R4 = Resistor [tolerance=±5% resistance=1k package=THT]
  R5 = Resistor [tolerance=±5% resistance=4.7k package=THT]
  BAT1 = Battery Holders [package=battcon_12mm_pth]

nets:
  N1: Componente1.A0, R3.Pin_0
  N2: Componente1.A1, R4.Pin_0, R5.Pin_0
  N3: Componente1.A3, LCD1.pin_5
  N4: Componente1.A4, LCD1.pin3
  N5: Componente1.A5, LCD1.pin_7
  N6: Componente1.A7, LCD1.pin_6
  N7: Componente1.3V3, LCD1.pin_1, LCD1.pin_8, R2.Pin_1, D1.C
  N8: Componente1.GND2, LCD1.pin2, J1.pin1, R1.pin_0, S1.1, S2.1, S3.1, R4.Pin_1, BAT1.+
  N9: Componente1.A9, Q2.Gate
  N10: Componente1.A8, Q1.Gate
  N11: Componente1.B15, J1.pin2
  N12: Componente1.A2, LCD1.pin4
  N13: R1.pin_1, R2.Pin_0, R3.Pin_1, D1.A
  N14: R5.Pin_1, BAT1.-

custom parts:
  TFT 1.8 inch 160x128 w SD: This is a generic 1.8 tft spi lcd display available on ebay and others. The 1.8" display has 128x160 color pixels.
