# Fritzing sketch esquematico_moskvich (saved by Fritzing 0.9.3b)
breadboards: 2

parts:
  Componente1 = BluePill
  J1 = Piezo Speaker
  R1 = Temperature Sensor (Thermistor) [thermistor_type=NTC package=THT]
  R2 = Resistor [tolerance=±5% resistance=6.75k package=THT]
  Config = SWITCH-MOMENTARY-2 [package=tactile-pth-12mm]
  R3 = Resistor [tolerance=±5% resistance=4.7k package=THT]
  D1 = Diode [package=diode-hv]
  R4 = Resistor [tolerance=±5% resistance=560 package=THT]
  R5 = Resistor [tolerance=±5% resistance=240 package=THT]
  JP1 = RCA [package=rca]
  Q1 = NPN-Transistor [package="TO92 [THT]"]
  D2 = Diode [package=diode-hv]
  R6 = Resistor [tolerance=±5% resistance=220 package=THT]
  R7 = Resistor [tolerance=±5% resistance=1k package=THT]
  R8 = Resistor [tolerance=±5% resistance=4.7k package=THT]
  R9 = Resistor [tolerance=±5% resistance=4.7k package=THT]
  R10 = Resistor [tolerance=±5% resistance=1k package=THT]
  Reversa = SWITCH-MOMENTARY-2 [package=tactile_switch_tall]
  C1 = Electrolytic Capacitor [capacitance=4.7µF package="100 mil [THT, electrolytic]"]
  C2 = Electrolytic Capacitor [capacitance=4.7µF package="100 mil [THT, electrolytic]"]
  C3 = Electrolytic Capacitor [capacitance=4.7µF package="100 mil [THT, electrolytic]"]
  Componente2 = u-blox NEO-6M GPS Breakout
  R11 = Resistor [tolerance=±5% resistance=2k package=THT]
  R12 = Resistor [tolerance=±5% resistance=4.7k package=THT]
  D3 = Zener Diode [part_number=1N4732A breakdown_voltage=3.3V package="300 mil [THT]"]
  C4 = Ceramic Capacitor [capacitance=5nF package="100 mil [THT, multilayer]"]
  BAT2 = 12 battery [package=battery]

nets:
  N1: Componente1.A0, R3.Pin_0, D1.A, C1.+
  N2: Componente1.A1, R4.Pin_0
  N3: Componente1.A7, R5.Pin_1
  N4: Componente1.B10, Componente2.RXD
  N5: Componente1.B11, Componente2.TXD
  3V3: Componente1.3V3, Componente2.VCC
  GND: Componente1.GND, Componente2.GND, R11.Pin_0, D3.anode, C4.1
  N6: Componente1.3V31, R2.Pin_1, D1.C
  N7: Componente1.B6, D2.A
  N8: Componente1.B5, R9.Pin_1, R10.Pin_0, C3.+
  N9: Componente1.A15, R11.Pin_1, R12.Pin_0, D3.cathode, C4.0
  N10: Componente1.A10, Config.2
  N11: Componente1.A2, R7.Pin_1, R8.Pin_1, C2.+
  N12: J1.pin1, Q1.C
  N13: J1.pin2, R8.Pin_0, Reversa.2, BAT2.+
  N14: R1.pin_0, Config.1, JP1.SHELL, Q1.E, R7.Pin_0, R10.Pin_1, C1.-, C2.-, C3.-, BAT2.-
  N15: R1.pin_1, R2.Pin_0, R3.Pin_1
  N16: R4.Pin_1, R5.Pin_0, JP1.PIN
  N17: Q1.B, R6.Pin_1
  N18: D2.C, R6.Pin_0
  N19: R9.Pin_0, Reversa.1

notes:
  Sensor de la reversa

custom parts:
  12 battery: 12V lead acid type battery, like the Husqvarna YTH2448 12V 35AH battery. This is the mini version 1/4 the size of the actual battery to be closer to typical breadboard parts (around 2in wide rathher than 7in). The pads in pcb are sized to accomidate up to 14ga wire (as these batterys will deliver high currents.)
