# Fritzing sketch Power_meter (saved by Fritzing 0.9.3b)
breadboards: 1

parts:
  OLED_I2C1 = OLED 128x64 I2C Monochrome Display
  R1 = Resistor [tolerance=±5% resistance=1M package=THT]
  R2 = Resistor [tolerance=±5% resistance=220k package=THT]
  R3 = Resistor [tolerance=±5% resistance=10k package=THT]
  JP1 = Header 2 [package=screwterminal-3.5mm-2_lock]
  Componente1 = BluePill
  R4 = Resistor [tolerance=±5% resistance=68k package=THT]
  R5 = Resistor [tolerance=±5% resistance=68k package=THT]
  C1 = Electrolytic Capacitor [capacitance=10µF package="100 mil [THT, electrolytic]"]
  C2 = Electrolytic Capacitor [capacitance=100µF package="200 mil [THT, electrolytic]"]
  Componente2 = ACS712 Low Current Sensor Board v12
  R6 = Resistor [tolerance=±5% resistance=330 package=THT]
  R7 = Resistor [tolerance=±5% resistance=330 package=THT]
  R8 = Resistor [tolerance=±5% resistance=4.7k package=THT]
  R9 = Resistor [tolerance=±5% resistance=4.7k package=THT]
  C3 = Ceramic Capacitor [capacitance=47nF package="100 mil [THT, multilayer]"]
  R10 = Resistor [tolerance=±5% resistance=1k package=THT]

nets:
  N1: OLED_I2C1.SDA, R7.Pin_0, R8.Pin_0
  N2: OLED_I2C1.SCK, R6.Pin_0, R9.Pin_0
  VDD: OLED_I2C1.VDD, Componente1.3V3, R4.Pin_0, R8.Pin_1, R9.Pin_1
  GND: OLED_I2C1.GND, Componente1.GND2, R5.Pin_1, C1.-, C3.1
  N3: R1.Pin_0, JP1.1
  N4: R1.Pin_1, R2.Pin_0
  N5: R2.Pin_1, R3.Pin_1, Componente1.A1
  N6: R3.Pin_0, JP1.2, R4.Pin_1, R5.Pin_0, C1.+
  N7: Componente1.A0, C3.0, R10.Pin_1
  GND_2: Componente1.GND, Componente2.GND
  N8: Componente1.3V31, C2.+, Componente2.5V
  N9: Componente1.GND3, C2.-
  N10: Componente1.B7, R7.Pin_1
  N11: Componente1.B6, R6.Pin_1
  N12: Componente2.VO, R10.Pin_0
