# Fritzing sketch Pump_controller (saved by Fritzing 0.9.3b)
breadboards: 1

parts:
  Componente1 = BluePill
  LCD1 = TFT 1.8 inch 160x128 w SD
  hc-sr1 = hc-sr04
  hc-sr2 = hc-sr04
  R1 = Resistor [tolerance=±5% resistance=4.7k package=THT]
  Q2 = LTR-301 [package=ltr-301]

nets:
  N1: Componente1.C15, R1.Pin_0, Q2.C
  N2: Componente1.A3, LCD1.pin_5
  N3: Componente1.A4, LCD1.pin3
  N4: Componente1.A5, LCD1.pin_7
  N5: Componente1.A7, LCD1.pin_6
  3V3: Componente1.3V3, LCD1.pin_1, LCD1.pin_8, hc-sr1.VCC, R1.Pin_1
  GND2: Componente1.GND2, LCD1.pin2, hc-sr1.GND, Q2.E
  N6: Componente1.A9, hc-sr2.Echo
  N7: Componente1.A8, hc-sr1.Echo
  N8: Componente1.B15, hc-sr1.Trig, hc-sr2.Trig
  N9: Componente1.A2, LCD1.pin4

custom parts:
  TFT 1.8 inch 160x128 w SD: This is a generic 1.8 tft spi lcd display available on ebay and others. The 1.8" display has 128x160 color pixels.
  LTR-301: Through-hole side-receiving IR phototransistor
