# Fritzing sketch Termometro (saved by Fritzing 0.9.3b)

parts:
  OLED1 = 128x64 Monochrom OLED Display with SPI Control
  Componente1 = BluePill
  U1 = MAX6675 [package=so08]

nets:
  N1: OLED1.Data, Componente1.B6
  N2: OLED1.Clock, Componente1.B7
  N3: OLED1.SA0/DC, Componente1.B8
  N4: OLED1.Reset, Componente1.B9
  GND: OLED1.CS, OLED1.GND, Componente1.GND3
  N5: OLED1.3v3, Componente1.3V31
  3V3: Componente1.3V3, U1.VDD
  GND2: Componente1.GND2, U1.VSS
  N6: Componente1.A10, U1.SCK
  N7: Componente1.A9, U1.CS
  N8: Componente1.A8, U1.MISO
